# Fritzing sketch algorithimc (saved by Fritzing 1.0.4)

parts:
  Part1 = Arduino Nano (Rev3.0)
  Pololu_A1 = Pololu A4988 [package=SO16]
  Pololu_A2 = Pololu A4988 [package=SO16]
  J4 = male pin header, 4 pins [form="♂ (male)"]
  J3 = male pin header, 4 pins [form="♂ (male)"]
  Buttons_connector = male pin header, 10 pins [form="♂ (male)"]
  REMOVE_button = male pin header, 1 pin [form="♂ (male)"]
  J5 = Screw terminal - 2 pins [package=THT]
  WS2812b_connector = male pin header, 3 pins [form="♂ (male)"]
  I2C_screen = male pin header, 4 pins [form="♂ (male)"]

nets:
  N1: Part1.D2, WS2812b_connector.pin1
  N2: Part1.D3, Buttons_connector.pin1
  N3: Part1.D4, Buttons_connector.pin2
  N4: Part1.D5, Buttons_connector.pin3
  N5: Part1.D6, Buttons_connector.pin4
  N6: Part1.D7, Buttons_connector.pin5
  N7: Part1.D8, Buttons_connector.pin6
  N8: Part1.D9, Buttons_connector.pin7
  N9: Part1.D10, Buttons_connector.pin8
  N10: Part1.D11/MOSI, Buttons_connector.pin9
  N11: Part1.D12/MISO, Buttons_connector.pin10
  N12: Part1.VIN, Pololu_A1.VMOT, Pololu_A2.VMOT, J5.pin1
  GND: Part1.GND, Pololu_A1.GND, Pololu_A2.GND, J5.pin2, WS2812b_connector.pin2, I2C_screen.pin2
  VDD: Part1.5V, Pololu_A1.MS2, Pololu_A1.VDD, Pololu_A2.MS2, Pololu_A2.VDD, WS2812b_connector.pin3, I2C_screen.pin1
  N13: Part1.A7, REMOVE_button.pin1
  N14: Part1.A5, I2C_screen.pin3
  N15: Part1.A4, I2C_screen.pin4
  N16: Part1.A3, Pololu_A2.DIR
  N17: Part1.A2, Pololu_A2.STEP
  N18: Part1.A1, Pololu_A1.DIR
  N19: Part1.A0, Pololu_A1.STEP
  N20: Part1.D13/SCK, Pololu_A1.ENABLE, Pololu_A2.ENABLE
  N21: Pololu_A1.RESET, Pololu_A1.SLEEP
  N22: Pololu_A1.1B, J3.pin4
  N23: Pololu_A1.1A, J3.pin3
  N24: Pololu_A1.2A, J3.pin2
  N25: Pololu_A1.2B, J3.pin1
  N26: Pololu_A2.RESET, Pololu_A2.SLEEP
  N27: Pololu_A2.1B, J4.pin4
  N28: Pololu_A2.1A, J4.pin3
  N29: Pololu_A2.2A, J4.pin2
  N30: Pololu_A2.2B, J4.pin1
